# Fritzing sketch main (saved by Fritzing 0.9.3b)
circuit board: 8.46667cm x 5.64444cm
breadboards: 1

parts:
  LED = LED - 5mm [color="Red (633nm)" package="5 mm [THT]"]
  R1 = Resistor [tolerance=±5% resistance=220 package=THT]
  Buzzer = Piezo Speaker
  R3 = Resistor [tolerance=±5% resistance=220 package=THT]
  DHT22 = Humidity and Temperature Sensor RHT03
  Raspberry_Pi_3 = Raspberry Pi 3 [part_number=RPI-3-V1.2]
  R2 = Resistor [tolerance=±5% resistance=220 package=THT]

nets:
  N1: LED.cathode, R1.Pin_1
  N2: LED.anode, Raspberry_Pi_3.GPIO27
  N3: R1.Pin_0, R3.Pin_0, Raspberry_Pi_3.GND, R2.Pin_0
  N4: Buzzer.pin1, R2.Pin_1
  N5: Buzzer.pin2, Raspberry_Pi_3.GPIO17
  N6: R3.Pin_1, DHT22.GND_2
  3V3: DHT22.Vcc, Raspberry_Pi_3.3v3, Raspberry_Pi_3.3V3
  N7: DHT22.Data-signal, Raspberry_Pi_3.GPIO4
